// Logisim project bfProcessor.circ as structural Verilog: 15 circuits, main circuit main
module main (
);

  wire clock_1_out, keyboard_1_avail, machine_1_read_kyb, machine_1_terminal_out;
  wire [6:0] keyboard_1_data, machine_1_ascii_out;
  wire [15:0] machine_1_rom_address;
  wire [19:0] rom_1_data;

  Keyboard keyboard_1 (
    .clk(clock_1_out), .re(machine_1_read_kyb), .avail(keyboard_1_avail), .data(keyboard_1_data));  // open: clr
  TTY tty_1 (.data(machine_1_ascii_out), .clk(clock_1_out), .we(machine_1_terminal_out));  // open: clr
  ROM #(.addrWidth(16), .dataWidth(20)) rom_1 (.addr(machine_1_rom_address), .data(rom_1_data));  // open: sel
  Clock_part clock_1 (.out(clock_1_out));
  Machine machine_1 (
    .READ_KYB(machine_1_read_kyb), .ASCII_IN(keyboard_1_data), .KYB_AVAIL(keyboard_1_avail),
    .ROM_ADDRESS(machine_1_rom_address), .DATA_IN(rom_1_data), .ASCII_OUT(machine_1_ascii_out),
    .CLOCK(clock_1_out), .TERMINAL_OUT(machine_1_terminal_out));  // open: TERMINAL_CLEAR

  // Notes on the sheet:
  //   contents of rom_1 (hex, n*v repeats v):
  //   8*10000 40000 80000 a0000 50000 20000 4*10000 40000 80000 a0000 50000 20000 10000 10000 40000 50000
  //   20000 10000 10000 10000 40000 50000 20000 10000 10000 10000 40000 50000 20000 10000 40000 4*50001
  //   20000 10001 40000 b0000 90000 50000 20000 10000 40000 50000 20000 10000 40000 50000 20000 10001
  //   40000 50000 50000 20000 10000 40000 80000 a0000 50001 20000 b0000 90000 50001 20000 10001 40000
  //   b0000 90000 50000 50000 20000 c0000 50000 20000 10001 10001 10001 40000 c0000 7*10000 40000 c0000
  //   c0000 10000 10000 10000 40000 c0000 50000 50000 20000 c0000 50001 20000 10001 40000 c0000 50001
  //   20000 c0000 10000 10000 10000 40000 c0000 6*10001 40000 c0000 8*10001 40000 c0000 50000 50000 20000
  //   10000 40000 c0000 50000 20000 10000 10000 40000 c0000 e0000
endmodule

module Machine (
  input  [19:0] DATA_IN,
  input  [6:0] ASCII_IN,
  input  KYB_AVAIL,
  input  CLOCK,
  output [15:0] ROM_ADDRESS,
  output [6:0] ASCII_OUT,
  output TERMINAL_OUT,
  output TERMINAL_CLEAR,
  output READ_KYB
);

  wire cpu_2_1_1_load_ram, cpu_2_1_1_load_stack, cpu_2_1_1_store_ram, cpu_2_1_1_store_stack;
  wire [15:0] cpu_2_1_1_ram_address, cpu_2_1_1_ram_out, cpu_2_1_1_stack_address, ram_1_data, ram_2_data;

  RAM #(.addrWidth(16), .dataWidth(16), .bus("separate")) ram_1 (
    .addr(cpu_2_1_1_stack_address), .din(ROM_ADDRESS), .data(ram_1_data), .str(cpu_2_1_1_store_stack),
    .clk(CLOCK), .ld(cpu_2_1_1_load_stack));  // open: sel, clr
  CPU_2_1 cpu_2_1_1 (
    .STACK_IN(ram_1_data), .STACK_ADDRESS(cpu_2_1_1_stack_address), .STORE_STACK(cpu_2_1_1_store_stack),
    .LOAD_STACK(cpu_2_1_1_load_stack), .ROM_ADDRESS(ROM_ADDRESS), .ROM_IN(DATA_IN[19:16]),
    .Data(DATA_IN[15:0]), .ASCII_OUT(ASCII_OUT), .TERMINAL_OUT(TERMINAL_OUT),
    .TERMINAL_CLEAR(TERMINAL_CLEAR), .READ_KYB(READ_KYB), .ASCII_IN(ASCII_IN), .KYB_AVAIL(KYB_AVAIL),
    .CLOCK_IN(CLOCK), .STORE_RAM(cpu_2_1_1_store_ram), .RAM_OUT(cpu_2_1_1_ram_out), .RAM_IN(ram_2_data),
    .RAM_ADDRESS(cpu_2_1_1_ram_address), .LOAD_RAM(cpu_2_1_1_load_ram));
  RAM #(.addrWidth(16), .dataWidth(16), .bus("separate")) ram_2 (
    .addr(cpu_2_1_1_ram_address), .din(cpu_2_1_1_ram_out), .data(ram_2_data), .str(cpu_2_1_1_store_ram),
    .clk(CLOCK), .ld(cpu_2_1_1_load_ram));  // open: sel, clr
endmodule

module CPU_2_1 (
  input  [3:0] ROM_IN,
  input  [15:0] Data,
  input  [15:0] RAM_IN,
  input  [15:0] STACK_IN,
  input  [6:0] ASCII_IN,
  input  KYB_AVAIL,
  input  CLOCK_IN,
  output [15:0] ROM_ADDRESS,
  output [6:0] ASCII_OUT,
  output TERMINAL_OUT,
  output TERMINAL_CLEAR,
  output STORE_RAM,
  output [15:0] RAM_OUT,
  output [15:0] RAM_ADDRESS,
  output LOAD_RAM,
  output [15:0] STACK_ADDRESS,
  output STORE_STACK,
  output LOAD_STACK,
  output READ_KYB
);

  wire clock_1_clk_out, decoder_v2_1_1_gr, decoder_v2_1_1_gr_loadi, decoder_v2_1_1_halt,
       decoder_v2_1_1_print, decoder_v2_1_1_ptr, decoder_v2_1_1_ptr_ld, decoder_v2_1_1_ptr_ldi,
       decoder_v2_1_1_stack_load, decoder_v2_1_1_stack_minus_minus, decoder_v2_1_1_stack_plus_plus,
       decoder_v2_1_1_stack_store;

  DECODER_V2_1 decoder_v2_1_1 (
    .OpCode(ROM_IN), .HALT(decoder_v2_1_1_halt), .INPUT(READ_KYB), .PRINT(decoder_v2_1_1_print),
    .STACK_LOAD(decoder_v2_1_1_stack_load), .STACK_STORE(decoder_v2_1_1_stack_store),
    .STACK_minus_minus(decoder_v2_1_1_stack_minus_minus), .STACK_plus_plus(decoder_v2_1_1_stack_plus_plus),
    .PTR_LDi(decoder_v2_1_1_ptr_ldi), .PTR_LD(decoder_v2_1_1_ptr_ld), .PTR(decoder_v2_1_1_ptr),
    .GR_STORE(STORE_RAM), .GR_LOADi(decoder_v2_1_1_gr_loadi), .GR_LOAD(LOAD_RAM), .GR(decoder_v2_1_1_gr));
  Stack_New stack_new_1 (
    .STORE(decoder_v2_1_1_stack_store), .LOAD(decoder_v2_1_1_stack_load),
    .PTR_plus_plus(decoder_v2_1_1_stack_plus_plus), .PTR_minus_minus(decoder_v2_1_1_stack_minus_minus),
    .VAL(RAM_OUT), .KYB(KYB_AVAIL), .CLOCK(clock_1_clk_out), .HALT(READ_KYB), .ROM_PTR(ROM_ADDRESS),
    .PTR_IN(STACK_IN), .LOAD_OUT(LOAD_STACK), .STORE_OUT(STORE_STACK), .PTR_OUT(STACK_ADDRESS));
  Working_Register working_register_1 (
    .VAL(decoder_v2_1_1_gr), .VAL_minus_minus(Data[0]), .LOAD(LOAD_RAM), .LOADi(decoder_v2_1_1_gr_loadi),
    .DATA_IN(RAM_IN), .IMMEDIATE_IN(Data), .ASCII_IN(ASCII_IN), .LOAD_ASCII(READ_KYB),
    .CLOCK(clock_1_clk_out), .DATA_OUT(RAM_OUT));
  Memory_Controller memory_controller_1 (
    .PTR(decoder_v2_1_1_ptr), .PTR_minus_minus(Data[0]), .LOAD(decoder_v2_1_1_ptr_ld),
    .LOADi(decoder_v2_1_1_ptr_ldi), .PTR_IN(RAM_OUT), .IMMEDIATE_IN(Data), .CLOCK(clock_1_clk_out),
    .PTR_OUT(RAM_ADDRESS));
  Clock clock_1 (
    .HALT(decoder_v2_1_1_halt), .AWAIT(READ_KYB), .CONTINUE(KYB_AVAIL), .CLK_OUT(clock_1_clk_out),
    .CLK_IN(CLOCK_IN));
  Terminal_Controller terminal_controller_1 (
    .WRITE(decoder_v2_1_1_print), .Immediate(Data[0]), .Immediate_In(Data[7:1]), .Memory_In(RAM_OUT),
    .ASCII_OUT(ASCII_OUT), .WRITE_OUT(TERMINAL_OUT), .CLEAR(TERMINAL_CLEAR));
endmodule

// Decoder
module DECODER_V2_1 (
  input  [3:0] OpCode,
  output HALT,
  output INPUT,
  output PRINT,
  output STACK_LOAD,
  output STACK_STORE,
  output STACK_minus_minus,
  output STACK_plus_plus,
  output PTR_LDi,
  output PTR_LD,
  output PTR,
  output GR_STORE,
  output GR_LOADi,
  output GR_LOAD,
  output GR
);

  wire nor_1_out, nor_2_out, nor_3_out, nor_4_out, nor_5_out, nor_6_out, nor_7_out, nor_8_out, not_1_out,
       not_2_out, not_3_out, not_4_out, not_5_out, not_6_out, not_7_out, not_8_out, not_9_out;

  and and_1 (HALT, OpCode[3], OpCode[2], OpCode[1], not_2_out);
  not not_1 (not_1_out, OpCode[1]);
  not not_2 (not_2_out, OpCode[0]);
  and and_2 (INPUT, OpCode[3], OpCode[2], OpCode[0], not_1_out);
  not not_3 (not_3_out, OpCode[2]);
  nor nor_1 (nor_1_out, OpCode[1], OpCode[0]);
  and and_3 (PRINT, OpCode[3], OpCode[2], nor_1_out);
  and and_4 (STACK_LOAD, OpCode[3], not_3_out, OpCode[1], OpCode[0]);
  not not_4 (not_4_out, OpCode[2]);
  nor nor_2 (nor_2_out, OpCode[2], OpCode[0]);
  and and_5 (STACK_STORE, OpCode[3], OpCode[1], nor_2_out);
  not not_5 (not_5_out, OpCode[1]);
  not not_6 (not_6_out, OpCode[2]);
  not not_7 (not_7_out, OpCode[1]);
  and and_6 (STACK_minus_minus, OpCode[3], not_4_out, not_7_out, OpCode[0]);
  and and_7 (STACK_plus_plus, OpCode[3], not_6_out, not_5_out, not_9_out);
  not not_8 (not_8_out, OpCode[3]);
  not not_9 (not_9_out, OpCode[0]);
  and and_8 (PTR_LDi, OpCode[0], OpCode[1], OpCode[2], not_8_out);
  nor nor_3 (nor_3_out, OpCode[3], OpCode[0]);
  nor nor_4 (nor_4_out, OpCode[3], OpCode[1]);
  and and_9 (PTR_LD, OpCode[2], OpCode[1], nor_3_out);
  and and_10 (PTR, OpCode[2], OpCode[0], nor_4_out);
  nor nor_5 (nor_5_out, OpCode[3], OpCode[1], OpCode[0]);
  and and_11 (GR_LOADi, OpCode[1], OpCode[0], nor_7_out);
  and and_12 (GR_STORE, OpCode[2], nor_5_out);
  nor nor_6 (nor_6_out, OpCode[3], OpCode[2], OpCode[0]);
  nor nor_7 (nor_7_out, OpCode[3], OpCode[2]);
  nor nor_8 (nor_8_out, OpCode[3], OpCode[2], OpCode[1]);
  and and_13 (GR_LOAD, OpCode[1], nor_6_out);
  and and_14 (GR, nor_8_out, OpCode[0]);
endmodule

// Register
module Working_Register (
  input  VAL,
  input  VAL_minus_minus,
  input  LOAD,
  input  LOADi,
  input  [15:0] DATA_IN,
  input  [15:0] IMMEDIATE_IN,
  input  [6:0] ASCII_IN,
  input  LOAD_ASCII,
  input  CLOCK,
  output [15:0] DATA_OUT
);

  wire and_1_out, or_1_out, or_2_out;
  wire [15:0] and_2_out, and_3_out, and_4_out, bit_extender_1_out, bit_extender_2_out, bit_extender_3_out,
       bit_extender_4_out, or_3_out;

  and and_1 (and_1_out, VAL, VAL_minus_minus);
  assign bit_extender_1_out = {{15{LOAD}}, LOAD};  // Bit_Extender bit_extender_1
  assign bit_extender_2_out = {{15{LOADi}}, LOADi};  // Bit_Extender bit_extender_2
  assign bit_extender_3_out = {{9{1'b0}}, ASCII_IN};  // Bit_Extender bit_extender_3
  or or_1 (or_1_out, LOAD, LOAD_ASCII, LOADi);
  assign and_2_out = bit_extender_1_out & DATA_IN;  // AND_Gate and_2, 16 bits wide
  assign and_3_out = bit_extender_2_out & IMMEDIATE_IN;  // AND_Gate and_3, 16 bits wide
  assign and_4_out = bit_extender_3_out & bit_extender_4_out;  // AND_Gate and_4, 16 bits wide
  assign bit_extender_4_out = {{15{LOAD_ASCII}}, LOAD_ASCII};  // Bit_Extender bit_extender_4
  or or_2 (or_2_out, or_1_out, and_1_out);
  assign or_3_out = and_2_out | and_4_out | and_3_out;  // OR_Gate or_3, 16 bits wide
  Counter #(.width(16), .max('hffff)) GR (
    .load(or_2_out), .D(or_3_out), .count(VAL), .Q(DATA_OUT), .clk(CLOCK));  // open: carry, clr
endmodule

// Output
module Terminal_Controller (
  input  WRITE,
  input  Immediate,
  input  [6:0] Immediate_In,
  input  [15:0] Memory_In,
  output [6:0] ASCII_OUT,
  output WRITE_OUT,
  output CLEAR
);

  wire and_4_out, comparator_1_eq, not_1_out;
  wire [6:0] and_1_out, and_2_out, bit_extender_1_out, bit_extender_2_out;

  assign bit_extender_1_out = {{6{Immediate}}, Immediate};  // Bit_Extender bit_extender_1
  not not_1 (not_1_out, Immediate);
  assign bit_extender_2_out = {{6{not_1_out}}, not_1_out};  // Bit_Extender bit_extender_2
  assign ASCII_OUT = and_1_out | and_2_out;  // OR_Gate or_1, 7 bits wide
  assign and_1_out = bit_extender_1_out & Immediate_In;  // AND_Gate and_1, 7 bits wide
  assign and_2_out = bit_extender_2_out & Memory_In[6:0];  // AND_Gate and_2, 7 bits wide
  or or_2 (WRITE_OUT, Immediate, WRITE);
  and and_3 (CLEAR, WRITE, and_4_out);
  and and_4 (and_4_out, Immediate, comparator_1_eq);
  Comparator #(.width(7)) comparator_1 (.a({7{1'b0}}), .b(and_1_out), .eq(comparator_1_eq));  // open: gt, lt
endmodule

// Stack
module Stack_New (
  input  [15:0] VAL,
  input  KYB,
  input  [15:0] PTR_IN,
  input  STORE,
  input  LOAD,
  input  PTR_plus_plus,
  input  PTR_minus_minus,
  input  CLOCK,
  input  HALT,
  output LOAD_OUT,
  output STORE_OUT,
  output [15:0] PTR_OUT,
  output [15:0] ROM_PTR
);

  wire and_2_out, and_3_out, comparator_1_eq, not_1_out, not_2_out, not_3_out, or_1_out, or_2_out;

  Comparator #(.width(16)) comparator_1 (.a(VAL), .b({16{1'b0}}), .eq(comparator_1_eq));  // open: gt, lt
  not not_1 (not_1_out, comparator_1_eq);
  and and_1 (LOAD_OUT, not_1_out, LOAD);
  and and_2 (and_2_out, PTR_minus_minus, comparator_1_eq);
  Counter #(.width(16), .max('hffff)) ADR (
    .load(and_2_out), .count(or_1_out), .Q(PTR_OUT), .clk(CLOCK));  // open: D, carry, clr
  or or_1 (or_1_out, and_2_out, PTR_plus_plus);
  not not_2 (not_2_out, KYB);
  and and_3 (and_3_out, HALT, not_2_out);
  or or_2 (or_2_out, LOAD_OUT, and_3_out);
  not not_3 (not_3_out, or_2_out);
  Counter #(.width(16), .max('hffff)) PC (
    .load(LOAD_OUT), .D(PTR_IN), .count(not_3_out), .Q(ROM_PTR), .clk(CLOCK));  // open: carry, clr

  assign STORE_OUT = STORE;
endmodule

// Pointer
module Memory_Controller (
  input  PTR,
  input  PTR_minus_minus,
  input  LOAD,
  input  LOADi,
  input  [15:0] PTR_IN,
  input  [15:0] IMMEDIATE_IN,
  input  CLOCK,
  output [15:0] PTR_OUT
);

  wire and_1_out, not_1_out, or_1_out, or_2_out;
  wire [15:0] and_2_out, and_3_out, bit_extender_1_out, bit_extender_2_out, or_3_out;

  and and_1 (and_1_out, PTR, PTR_minus_minus);
  not not_1 (not_1_out, LOADi);
  assign bit_extender_1_out = {{15{not_1_out}}, not_1_out};  // Bit_Extender bit_extender_1
  assign bit_extender_2_out = {{15{LOADi}}, LOADi};  // Bit_Extender bit_extender_2
  or or_1 (or_1_out, LOAD, LOADi);
  assign and_2_out = bit_extender_1_out & PTR_IN;  // AND_Gate and_2, 16 bits wide
  assign and_3_out = bit_extender_2_out & IMMEDIATE_IN;  // AND_Gate and_3, 16 bits wide
  or or_2 (or_2_out, or_1_out, and_1_out);
  assign or_3_out = and_2_out | and_3_out;  // OR_Gate or_3, 16 bits wide
  Counter #(.width(16), .max('hffff)) GR (
    .load(or_2_out), .D(or_3_out), .count(PTR), .Q(PTR_OUT), .clk(CLOCK));  // open: carry, clr
endmodule

module Clock (
  input  HALT,
  input  AWAIT,
  input  CONTINUE,
  input  CLK_IN,
  output CLK_OUT
);

  wire j_k_ff_1_qn, not_1_out;

  and and_1 (CLK_OUT, not_1_out, j_k_ff_1_qn, CLK_IN);
  not not_1 (not_1_out, HALT);
  J_K_Flip_Flop j_k_ff_1 (.J(AWAIT), .clk(CLK_IN), .K(CONTINUE), .Qn(j_k_ff_1_qn));  // open: Q, preset, en, reset
endmodule

module UPDATED_MAIN (
);

  wire clock_1_out, keyboard_1_avail, v2_1_1_load_ram, v2_1_1_load_stack, v2_1_1_read_kyb, v2_1_1_store_ram,
       v2_1_1_store_stack, v2_1_1_terminal_clear, v2_1_1_terminal_out;
  wire [6:0] keyboard_1_data, v2_1_1_ascii_out;
  wire [15:0] ram_1_data, ram_2_data, v2_1_1_ram_address, v2_1_1_ram_out, v2_1_1_rom_address,
       v2_1_1_stack_address;
  wire [19:0] rom_1_data;

  ROM #(.addrWidth(16), .dataWidth(20)) rom_1 (.addr(v2_1_1_rom_address), .data(rom_1_data));  // open: sel
  Keyboard keyboard_1 (
    .clk(clock_1_out), .re(v2_1_1_read_kyb), .avail(keyboard_1_avail), .data(keyboard_1_data));  // open: clr
  RAM #(.addrWidth(16), .dataWidth(16), .bus("separate")) ram_1 (
    .addr(v2_1_1_stack_address), .din(v2_1_1_rom_address), .data(ram_1_data), .str(v2_1_1_store_stack),
    .clk(clock_1_out), .ld(v2_1_1_load_stack));  // open: sel, clr
  UPDATED_ft_STACK updated_ft_stack_1 ();  // open: STACK_IN, STACK_ADDRESS, STORE_STACK, LOAD_STACK, ROM_ADDRESS, ROM_IN, Data, ASCII_OUT, TERMINAL_OUT, TERMINAL_CLEAR, READ_KYB, ASCII_IN, KYB_AVAIL, CLOCK_IN, STORE_RAM, RAM_OUT, RAM_IN, RAM_ADDRESS, LOAD_RAM
  Clock_part clock_1 (.out(clock_1_out));
  V2_1 v2_1_1 (
    .STACK_IN(ram_1_data), .STACK_ADDRESS(v2_1_1_stack_address), .STORE_STACK(v2_1_1_store_stack),
    .LOAD_STACK(v2_1_1_load_stack), .ROM_ADDRESS(v2_1_1_rom_address), .ROM_IN(rom_1_data[19:16]),
    .Data(rom_1_data[15:0]), .ASCII_OUT(v2_1_1_ascii_out), .TERMINAL_OUT(v2_1_1_terminal_out),
    .TERMINAL_CLEAR(v2_1_1_terminal_clear), .READ_KYB(v2_1_1_read_kyb), .ASCII_IN(keyboard_1_data),
    .KYB_AVAIL(keyboard_1_avail), .CLOCK_IN(clock_1_out), .STORE_RAM(v2_1_1_store_ram),
    .RAM_OUT(v2_1_1_ram_out), .RAM_IN(ram_2_data), .RAM_ADDRESS(v2_1_1_ram_address),
    .LOAD_RAM(v2_1_1_load_ram));
  TTY tty_1 (.data(v2_1_1_ascii_out), .clk(clock_1_out), .we(v2_1_1_terminal_out), .clr(v2_1_1_terminal_clear));
  RAM #(.addrWidth(16), .dataWidth(16), .bus("separate")) ram_2 (
    .addr(v2_1_1_ram_address), .din(v2_1_1_ram_out), .data(ram_2_data), .str(v2_1_1_store_ram),
    .clk(clock_1_out), .ld(v2_1_1_load_ram));  // open: sel, clr
endmodule

module UPDATED_V2_1 (
  input  [3:0] ROM_IN,
  input  [15:0] Data,
  input  [15:0] RAM_IN,
  input  [15:0] STACK_IN,
  input  [6:0] ASCII_IN,
  input  KYB_AVAIL,
  input  CLOCK_IN,
  output [15:0] ROM_ADDRESS,
  output [6:0] ASCII_OUT,
  output TERMINAL_OUT,
  output TERMINAL_CLEAR,
  output STORE_RAM,
  output [15:0] RAM_OUT,
  output [15:0] RAM_ADDRESS,
  output LOAD_RAM,
  output [15:0] STACK_ADDRESS,
  output STORE_STACK,
  output LOAD_STACK,
  output READ_KYB
);

  wire decoder_v2_1_1_gr, decoder_v2_1_1_gr_loadi, decoder_v2_1_1_halt, decoder_v2_1_1_print,
       decoder_v2_1_1_ptr, decoder_v2_1_1_ptr_ld, decoder_v2_1_1_ptr_ldi, decoder_v2_1_1_stack_load,
       decoder_v2_1_1_stack_minus_minus, decoder_v2_1_1_stack_plus_plus, decoder_v2_1_1_stack_store,
       stack_new_1_p1;

  DECODER_V2_1 decoder_v2_1_1 (
    .OpCode(ROM_IN), .HALT(decoder_v2_1_1_halt), .INPUT(READ_KYB), .PRINT(decoder_v2_1_1_print),
    .STACK_LOAD(decoder_v2_1_1_stack_load), .STACK_STORE(decoder_v2_1_1_stack_store),
    .STACK_minus_minus(decoder_v2_1_1_stack_minus_minus), .STACK_plus_plus(decoder_v2_1_1_stack_plus_plus),
    .PTR_LDi(decoder_v2_1_1_ptr_ldi), .PTR_LD(decoder_v2_1_1_ptr_ld), .PTR(decoder_v2_1_1_ptr),
    .GR_STORE(STORE_RAM), .GR_LOADi(decoder_v2_1_1_gr_loadi), .GR_LOAD(LOAD_RAM), .GR(decoder_v2_1_1_gr));
  // Stack_New stack_new_1: pin names not known; wires that end beside it: stack_new_1_p1, decoder_v2_1_1_stack_minus_minus, STACK_ADDRESS, decoder_v2_1_1_stack_plus_plus, STORE_STACK, decoder_v2_1_1_stack_load, LOAD_STACK, decoder_v2_1_1_stack_store, STACK_IN, RAM_OUT
  Working_Register working_register_1 (
    .VAL(decoder_v2_1_1_gr), .VAL_minus_minus(Data[0]), .LOAD(LOAD_RAM), .LOADi(decoder_v2_1_1_gr_loadi),
    .DATA_IN(RAM_IN), .IMMEDIATE_IN(Data), .ASCII_IN(ASCII_IN), .LOAD_ASCII(READ_KYB),
    .CLOCK(stack_new_1_p1), .DATA_OUT(RAM_OUT));
  Memory_Controller memory_controller_1 (
    .PTR(decoder_v2_1_1_ptr), .PTR_minus_minus(Data[0]), .LOAD(decoder_v2_1_1_ptr_ld),
    .LOADi(decoder_v2_1_1_ptr_ldi), .PTR_IN(RAM_OUT), .IMMEDIATE_IN(Data), .CLOCK(stack_new_1_p1),
    .PTR_OUT(RAM_ADDRESS));
  Clock clock_1 (
    .HALT(decoder_v2_1_1_halt), .AWAIT(READ_KYB), .CONTINUE(KYB_AVAIL), .CLK_OUT(stack_new_1_p1),
    .CLK_IN(CLOCK_IN));
  Terminal_Controller terminal_controller_1 (
    .WRITE(decoder_v2_1_1_print), .Immediate(Data[0]), .Immediate_In(Data[7:1]), .Memory_In(RAM_OUT),
    .ASCII_OUT(ASCII_OUT), .WRITE_OUT(TERMINAL_OUT), .CLEAR(TERMINAL_CLEAR));
endmodule

module UPDATED_ft_STACK (
  input  [3:0] ROM_IN,
  input  [15:0] Data,
  input  [15:0] RAM_IN,
  input  [15:0] STACK_IN,
  input  [6:0] ASCII_IN,
  input  KYB_AVAIL,
  input  CLOCK_IN,
  output [15:0] ROM_ADDRESS,
  output [6:0] ASCII_OUT,
  output TERMINAL_OUT,
  output TERMINAL_CLEAR,
  output STORE_RAM,
  output [15:0] RAM_OUT,
  output [15:0] RAM_ADDRESS,
  output LOAD_RAM,
  output [15:0] STACK_ADDRESS,
  output STORE_STACK,
  output LOAD_STACK,
  output READ_KYB
);

  wire decoder_v2_1_gr, decoder_v2_1_gr_loadi, decoder_v2_1_halt, decoder_v2_1_print, decoder_v2_1_ptr,
       decoder_v2_1_ptr_ld, decoder_v2_1_ptr_ldi, stack_new_1_p3, stack_new_1_p5, stack_new_1_p7,
       stack_new_1_p9;

  DECODER_V2_1 decoder_v2_1_1 ();  // open: OpCode, HALT, INPUT, PRINT, STACK_LOAD, STACK_STORE, STACK_minus_minus, STACK_plus_plus, PTR_LDi, PTR_LD, PTR, GR_STORE, GR_LOADi, GR_LOAD, GR
  Clock clock_1 (
    .HALT(decoder_v2_1_halt), .AWAIT(READ_KYB), .CONTINUE(KYB_AVAIL), .CLK_OUT(ROM_ADDRESS[0]),
    .CLK_IN(CLOCK_IN));
  // Stack_New stack_new_1: pin names not known; wires that end beside it: ROM_ADDRESS, ROM_ADDRESS, stack_new_1_p3, STACK_ADDRESS, stack_new_1_p5, STORE_STACK, stack_new_1_p7, LOAD_STACK, stack_new_1_p9, STACK_IN, RAM_OUT
  DECODER_V2 decoder_v2_1 (
    .LOAD_STACK(stack_new_1_p7), .HALT(decoder_v2_1_halt), .OpCode(ROM_IN), .STACK_STORE(stack_new_1_p9),
    .INPUT(READ_KYB), .PRINT(decoder_v2_1_print), .STACK_minus_minus(stack_new_1_p3),
    .STACK_plus_plus(stack_new_1_p5), .PTR_LDi(decoder_v2_1_ptr_ldi), .PTR_LD(decoder_v2_1_ptr_ld),
    .PTR(decoder_v2_1_ptr), .GR_LOADi(decoder_v2_1_gr_loadi), .GR_LOAD(LOAD_RAM), .GR(decoder_v2_1_gr),
    .STORE_MEM(STORE_RAM));
  Working_Register working_register_1 (
    .VAL(decoder_v2_1_gr), .VAL_minus_minus(Data[0]), .LOAD(LOAD_RAM), .LOADi(decoder_v2_1_gr_loadi),
    .DATA_IN(RAM_IN), .IMMEDIATE_IN(Data), .ASCII_IN(ASCII_IN), .LOAD_ASCII(READ_KYB),
    .CLOCK(ROM_ADDRESS[0]), .DATA_OUT(RAM_OUT));
  Memory_Controller memory_controller_1 (
    .PTR(decoder_v2_1_ptr), .PTR_minus_minus(Data[0]), .LOAD(decoder_v2_1_ptr_ld),
    .LOADi(decoder_v2_1_ptr_ldi), .PTR_IN(RAM_OUT), .IMMEDIATE_IN(Data), .CLOCK(ROM_ADDRESS[0]),
    .PTR_OUT(RAM_ADDRESS));
  Terminal_Controller terminal_controller_1 (
    .WRITE(decoder_v2_1_print), .Immediate(Data[0]), .Immediate_In(Data[7:1]), .Memory_In(RAM_OUT),
    .ASCII_OUT(ASCII_OUT), .WRITE_OUT(TERMINAL_OUT), .CLEAR(TERMINAL_CLEAR));
  // Pins of 1 and 16 bits meet at ROM_ADDRESS
endmodule

module DECODER_V2 (
  input  [3:0] OpCode,
  output LOAD_STACK,
  output STORE_MEM,
  output HALT,
  output STACK_STORE,
  output INPUT,
  output PRINT,
  output STACK_minus_minus,
  output STACK_plus_plus,
  output PTR_LDi,
  output PTR_LD,
  output PTR,
  output GR_LOADi,
  output GR_LOAD,
  output GR
);

  wire nor_1_out, nor_2_out, nor_3_out, nor_4_out, nor_5_out, nor_6_out, nor_7_out, nor_8_out, not_1_out,
       not_2_out, not_3_out, not_4_out, not_5_out, not_6_out, not_7_out, not_8_out;

  and and_1 (LOAD_STACK, OpCode[3], nor_1_out, OpCode[1]);
  nor nor_1 (nor_1_out, OpCode[2], OpCode[0]);
  and and_2 (HALT, OpCode[1], OpCode[0], OpCode[3], not_3_out);
  not not_1 (not_1_out, OpCode[1]);
  not not_2 (not_2_out, OpCode[2]);
  not not_3 (not_3_out, OpCode[2]);
  and and_3 (STACK_STORE, OpCode[3], not_2_out, not_1_out, OpCode[0]);
  not not_4 (not_4_out, OpCode[2]);
  not not_5 (not_5_out, OpCode[0]);
  not not_6 (not_6_out, OpCode[1]);
  and and_4 (INPUT, OpCode[3], not_4_out, not_6_out, not_5_out);
  not not_7 (not_7_out, OpCode[3]);
  and and_5 (PRINT, OpCode[0], OpCode[1], OpCode[2], not_7_out);
  and and_6 (STACK_minus_minus, OpCode[2], OpCode[1], nor_2_out);
  nor nor_2 (nor_2_out, OpCode[3], OpCode[0]);
  nor nor_3 (nor_3_out, OpCode[3], OpCode[1]);
  and and_7 (STACK_plus_plus, OpCode[2], nor_3_out, OpCode[0]);
  not not_8 (not_8_out, OpCode[1]);
  nor nor_4 (nor_4_out, OpCode[3], OpCode[1], OpCode[0]);
  and and_8 (PTR_LDi, OpCode[0], OpCode[3], OpCode[2], not_8_out);
  and and_9 (PTR_LD, OpCode[2], nor_4_out);
  nor nor_5 (nor_5_out, OpCode[3], OpCode[2]);
  and and_10 (PTR, OpCode[1], OpCode[0], nor_5_out);
  nor nor_6 (nor_6_out, OpCode[3], OpCode[2], OpCode[0]);
  nor nor_7 (nor_7_out, OpCode[1], OpCode[0]);
  and and_11 (GR_LOADi, OpCode[3], OpCode[2], nor_7_out);
  and and_12 (GR_LOAD, OpCode[1], nor_6_out);
  nor nor_8 (nor_8_out, OpCode[3], OpCode[2], OpCode[1]);
  and and_13 (GR, nor_8_out, OpCode[0]);
  nor nor_9 (STORE_MEM, OpCode[3], OpCode[2], OpCode[1], OpCode[0]);
endmodule

module Stack_Controller (
  input  ADR,
  input  ADR_minus_minus,
  input  CLOCK,
  output [15:0] PTR_OUT
);

  wire and_1_out;

  and and_1 (and_1_out, ADR, ADR_minus_minus);
  Counter #(.width(16), .max('hffff)) u_ADR (
    .load(and_1_out), .count(ADR), .Q(PTR_OUT), .clk(CLOCK));  // open: D, carry, clr
endmodule

module V2_1 (
  input  [3:0] ROM_IN,
  input  [15:0] Data,
  input  [15:0] RAM_IN,
  input  [15:0] STACK_IN,
  input  [6:0] ASCII_IN,
  input  KYB_AVAIL,
  input  CLOCK_IN,
  output [15:0] ROM_ADDRESS,
  output [6:0] ASCII_OUT,
  output TERMINAL_OUT,
  output TERMINAL_CLEAR,
  output STORE_RAM,
  output [15:0] RAM_OUT,
  output [15:0] RAM_ADDRESS,
  output LOAD_RAM,
  output [15:0] STACK_ADDRESS,
  output STORE_STACK,
  output LOAD_STACK,
  output READ_KYB
);

  wire clock_1_clk_out, decoder_v2_1_1_gr, decoder_v2_1_1_gr_loadi, decoder_v2_1_1_halt,
       decoder_v2_1_1_print, decoder_v2_1_1_ptr, decoder_v2_1_1_ptr_ld, decoder_v2_1_1_ptr_ldi,
       decoder_v2_1_1_stack_load, decoder_v2_1_1_stack_minus_minus, decoder_v2_1_1_stack_plus_plus,
       decoder_v2_1_1_stack_store, stack_new_1_p1, stack_new_1_p2;

  DECODER_V2_1 decoder_v2_1_1 (
    .OpCode(ROM_IN), .HALT(decoder_v2_1_1_halt), .INPUT(READ_KYB), .PRINT(decoder_v2_1_1_print),
    .STACK_LOAD(decoder_v2_1_1_stack_load), .STACK_STORE(decoder_v2_1_1_stack_store),
    .STACK_minus_minus(decoder_v2_1_1_stack_minus_minus), .STACK_plus_plus(decoder_v2_1_1_stack_plus_plus),
    .PTR_LDi(decoder_v2_1_1_ptr_ldi), .PTR_LD(decoder_v2_1_1_ptr_ld), .PTR(decoder_v2_1_1_ptr),
    .GR_STORE(STORE_RAM), .GR_LOADi(decoder_v2_1_1_gr_loadi), .GR_LOAD(LOAD_RAM), .GR(decoder_v2_1_1_gr));
  // Stack_New stack_new_1: pin names not known; wires that end beside it: stack_new_1_p1, stack_new_1_p2, decoder_v2_1_1_stack_minus_minus, STACK_ADDRESS, decoder_v2_1_1_stack_plus_plus, STORE_STACK, decoder_v2_1_1_stack_load, LOAD_STACK, decoder_v2_1_1_stack_store, STACK_IN, RAM_OUT
  Working_Register working_register_1 (
    .VAL(decoder_v2_1_1_gr), .VAL_minus_minus(Data[0]), .LOAD(LOAD_RAM), .LOADi(decoder_v2_1_1_gr_loadi),
    .DATA_IN(RAM_IN), .IMMEDIATE_IN(Data), .ASCII_IN(ASCII_IN), .LOAD_ASCII(READ_KYB),
    .CLOCK(stack_new_1_p1), .DATA_OUT(RAM_OUT));
  Memory_Controller memory_controller_1 (
    .PTR(decoder_v2_1_1_ptr), .PTR_minus_minus(Data[0]), .LOAD(decoder_v2_1_1_ptr_ld),
    .LOADi(decoder_v2_1_1_ptr_ldi), .PTR_IN(RAM_OUT), .IMMEDIATE_IN(Data), .CLOCK(clock_1_clk_out),
    .PTR_OUT(RAM_ADDRESS));
  Clock clock_1 (
    .HALT(decoder_v2_1_1_halt), .AWAIT(READ_KYB), .CONTINUE(KYB_AVAIL), .CLK_OUT(clock_1_clk_out),
    .CLK_IN(CLOCK_IN));
  Terminal_Controller terminal_controller_1 (
    .WRITE(decoder_v2_1_1_print), .Immediate(Data[0]), .Immediate_In(Data[7:1]), .Memory_In(RAM_OUT),
    .ASCII_OUT(ASCII_OUT), .WRITE_OUT(TERMINAL_OUT), .CLEAR(TERMINAL_CLEAR));
endmodule
